# Fritzing sketch SRT (saved by Fritzing 0.8.4b)
breadboards: 1

parts:
  元件1 = Arduino Nano (Rev3.0)
  R1 = Resistor [package="2010 [SMD]"]
  R2 = Resistor [package="2010 [SMD]"]
  元件2 = Arduino Nano (Rev3.0)
  R3 = Resistor [package="2010 [SMD]"]
  R4 = Resistor [package="2010 [SMD]"]

nets:
  GND: 元件1.D1/TX, 元件1.GND, 元件1.D11/MOSI, 元件2.D1/TX, 元件2.GND, 元件2.D11/MOSI
  N1: 元件1.RESET, 元件1.D13/SCK, 元件2.RESET, 元件2.D13/SCK
  N2: 元件1.D10, 元件2.D10
  N3: 元件1.D12/MISO, 元件2.D12/MISO
  5V: 元件1.5V, 元件2.VIN
  N4: 元件1.A5, R1.Pin_0
  N5: 元件1.A4, R2.Pin_0
  N6: 元件1.3V3, R1.Pin_1, R2.Pin_1, R3.Pin_1, R4.Pin_1
  N7: 元件2.A5, R3.Pin_0
  N8: 元件2.A4, R4.Pin_0
